# Fritzing sketch Vacuum Pump Circuit_v4 (saved by Fritzing 0.9.3b)
breadboards: 1

parts:
  Switch_One = Toggle Switch [package=THT]
  Splashback_Diode = Rectifier Diode [part_number=1N4001 package="300 mil [THT]"]
  NPN_2222A_Transistor = NPN-Transistor [package="TO92 [THT]"]
  R1 = Resistor [tolerance=±5% resistance=220 package=THT]
  LED1 = LED - 5mm [color="Red (633nm)" package="5 mm [THT]"]
  M1 = DC Motor
  Power_plug1 = Power plug
  R2 = Resistor [tolerance=±5% resistance=220 package=THT]

nets:
  N1: Switch_One.L1, Splashback_Diode.cathode, M1.pin_1, Power_plug1.VCC
  N2: Switch_One.COM, R1.Pin_0, R2.Pin_0
  N3: Splashback_Diode.anode, NPN_2222A_Transistor.C, M1.pin_2
  N4: NPN_2222A_Transistor.E, R1.Pin_1, LED1.cathode, LED1.anode, Power_plug1.GND
  N5: NPN_2222A_Transistor.B, R2.Pin_1
